// Logisim project Matriz de LED 08xn - Informação Circulando.circ as structural Verilog: 1 circuit, main circuit main
module main (
  input  in_1
);

  wire and_1_out, Clear, clock_1_out;
  wire [8:0] _00, _01, _02, _03, _04, _05, _06, _07, _08, _09, _10, _11, _12, _13, _14, _15, _16, _17, _18,
       _19, _20, _21, _22, _23, _24, _25, _26, _27, _28, _29, _30, _31, rom_1_data;
  wire [9:0] counter_1_q;

  Button button_1 (.out(Clear));
  Clock clock_1 (.out(clock_1_out));
  // Probe on counter_1_q
  Counter #(.width(10), .max('h50)) counter_1 (
    .load(Clear), .count(in_1), .Q(counter_1_q), .clk(and_1_out));  // open: D, carry, clr
  and and_1 (and_1_out, in_1, clock_1_out);
  ROM #(.addrWidth(10), .dataWidth(9)) rom_1 (.addr(counter_1_q), .data(rom_1_data));  // open: sel
  Shift_Register #(.width(9), .length(32), .trigger("falling")) shift_register_1 (
    .shift(in_1), .in(rom_1_data), .clk(and_1_out), .clr(Clear), .q0(_00), .q1(_01), .q2(_02), .q3(_03),
    .q4(_04), .q5(_05), .q6(_06), .q7(_07), .q8(_08), .q9(_09), .q10(_10), .q11(_11), .q12(_12), .q13(_13),
    .q14(_14), .q15(_15), .q16(_16), .q17(_17), .q18(_18), .q19(_19), .q20(_20), .q21(_21), .q22(_22),
    .q23(_23), .q24(_24), .q25(_25), .q26(_26), .q27(_27), .q28(_28), .q29(_29), .q30(_30), .q31(_31));  // open: out, load, d0, d1, d2, d3, d4, d5, d6, d7, d8, d9, d10, d11, d12, d13, d14, d15, d16, d17, d18, d19, d20, d21, d22, d23, d24, d25, d26, d27, d28, d29, d30, d31
  DotMatrix #(.matrixcols(32), .matrixrows(9)) dotmatrix_1 (
    .col0(_31), .col1(_30), .col2(_29), .col3(_28), .col4(_27), .col5(_26), .col6(_25), .col7(_24),
    .col8(_23), .col9(_22), .col10(_21), .col11(_20), .col12(_19), .col13(_18), .col14(_17), .col15(_16),
    .col16(_15), .col17(_14), .col18(_13), .col19(_12), .col20(_11), .col21(_10), .col22(_09), .col23(_08),
    .col24(_07), .col25(_06), .col26(_05), .col27(_04), .col28(_03), .col29(_02), .col30(_01), .col31(_00));

  // Other names for the same wires on the sheet: On_Off = in_1

  // Notes on the sheet:
  //   Nome Circulando
  //   Prof.: Santiago Sinezio
  //   Copyrigth (c) 2020 David Gomesh
  //   Disciplina: Org. e Arq. de Computadores. 
  //   IFMA - Monte Castelo
  //   contents of rom_1 (hex, n*v repeats v):
  //   0 7e 42 42 3c 0 3e 48 48 3e 0 78 4 2 4 78 0 7e 0 7e 42 42 3c 5*0 3c 42 52 5c 0 3c 42 42 3c 0 7e 20
  //   10 20 7e 0 7e 52 52 52 0 72 52 52 5e 0 7e 10 10 7e
endmodule
